// Logisim project RISC-V.circ as structural Verilog: 11 circuits, main circuit main
module main (
  input  in_1
);

  wire and_1_out, and_2_out, AUIPC, branch_evaluator_1_out_4, clock_1_out, comparator_1_eq, comparator_2_eq,
       comparator_3_eq, comparator_4_eq, JAL, JALR, ld, LUI, not_1_out, not_2_out, not_3_out, not_4_out,
       not_5_out, not_6_out, not_7_out, not_8_out, not_9_out, not_10_out, not_11_out, not_12_out, not_13_out,
       not_14_out, or_1_out, or_2_out, register_write_1_out_2, st;
  wire [2:0] funct3;
  wire [4:0] immediate_decoder_1_rd, immediate_decoder_1_rs1, immediate_decoder_1_rs2, multiplexer_1_out,
       multiplexer_2_out;
  wire [6:0] funct7, opcode;
  wire [11:0] immediate_decoder_1_i, immediate_decoder_1_s;
  wire [12:0] immediate_decoder_1_b;
  wire [19:0] immediate_decoder_1_u;
  wire [23:0] counter_1_q, transistor_1_out_2;
  wire [31:0] adder_1_out, adder_2_out, adder_3_out, adder_4_out, adder_5_out, adder_6_out, alu_1_out_6,
       bit_extender_1_out, data_in_stapler_1_combined_data, data_out_slicer_1_out_4, Ii32b,
       immediate_decoder_1_j, multiplexer_3_out, multiplexer_4_out, multiplexer_5_out, multiplexer_6_out,
       multiplexer_7_out, multiplexer_8_out, multiplexer_9_out, ram_1_data, ram_2_data, ram_3_data,
       register_1_q, register_2_q, rom_1_data, Si32b, transistor_1_out, transistor_5_out;

  Clock clock_1 (.out(clock_1_out));
  LUI_AUIPC_JAL_JALR lui_auipc_jal_jalr_1 (
    .in_1(opcode), .JALR(JALR), .JAL(JAL), .AUIPC(AUIPC), .LUI(LUI), .Load(ld), .Store(st));
  and and_1 (and_1_out, clock_1_out, not_2_out);
  not not_1 (not_1_out, clock_1_out);
  not not_2 (not_2_out, not_1_out);
  Transistor #(.\type ("n"), .gate("br"), .width(32)) transistor_1 (
    .in(32'h10160), .out({transistor_1_out[31:26], transistor_1_out_2, transistor_1_out[1:0]}), .gate(in_1));
  Transistor #(.\type ("n"), .gate("br"), .width(32)) transistor_2 (
    .in(adder_5_out), .out({transistor_1_out[31:26], transistor_1_out_2, transistor_1_out[1:0]}), .gate(JALR));
  Counter #(.width(24), .max('hffffff), .trigger("falling")) counter_1 (
    .load(or_1_out), .D(transistor_1_out_2), .count(not_3_out), .Q(counter_1_q), .clk(and_1_out));  // open: carry, clr
  not not_3 (not_3_out, or_1_out);
  or or_1 (or_1_out, in_1, JAL, and_2_out, JALR);
  Transistor #(.\type ("n"), .gate("br"), .width(32)) transistor_3 (
    .in(adder_2_out), .out({transistor_1_out[31:26], transistor_1_out_2, transistor_1_out[1:0]}), .gate(JAL));
  not not_4 (not_4_out, clock_1_out);
  not not_5 (not_5_out, not_6_out);
  not not_6 (not_6_out, not_4_out);
  Transistor #(.\type ("n"), .gate("br"), .width(32)) transistor_4 (
    .in(adder_1_out), .out({transistor_1_out[31:26], transistor_1_out_2, transistor_1_out[1:0]}),
    .gate(and_2_out));
  not not_7 (not_7_out, not_5_out);
  not not_8 (not_8_out, not_9_out);
  not not_9 (not_9_out, not_7_out);
  ROM #(.addrWidth(24), .dataWidth(32)) rom_1 (.addr(counter_1_q), .data(rom_1_data));  // open: sel
  assign bit_extender_1_out = {{19{immediate_decoder_1_b[12]}}, immediate_decoder_1_b};  // Bit_Extender bit_extender_1
  Adder #(.width(32)) adder_1 (
    .a(bit_extender_1_out), .b({{6{1'b0}}, counter_1_q, 2'b00}), .out(adder_1_out));  // open: cin, cout
  Adder #(.width(32)) adder_2 (
    .a(immediate_decoder_1_j), .b({{6{1'b0}}, counter_1_q, 2'b00}), .out(adder_2_out));  // open: cin, cout
  not not_10 (not_10_out, not_8_out);
  immediate_decoder immediate_decoder_1 (
    .in_1(rom_1_data), .rd(immediate_decoder_1_rd), .rs1(immediate_decoder_1_rs1),
    .rs2(immediate_decoder_1_rs2), .funct3(funct3), .funct7(funct7), .I(immediate_decoder_1_i),
    .S(immediate_decoder_1_s), .B(immediate_decoder_1_b), .U(immediate_decoder_1_u),
    .J(immediate_decoder_1_j), .opcode(opcode));
  assign Ii32b = {{20{immediate_decoder_1_i[11]}}, immediate_decoder_1_i};  // Bit_Extender bit_extender_2
  assign Si32b = {{20{1'b0}}, immediate_decoder_1_s};  // Bit_Extender bit_extender_3
  Adder #(.width(32)) adder_3 (
    .a({immediate_decoder_1_u, {12{1'b0}}}), .b({{6{1'b0}}, counter_1_q, 2'b00}), .out(adder_3_out));  // open: cin, cout
  Adder #(.width(32)) adder_4 (.a({{6{1'b0}}, counter_1_q, 2'b00}), .b(32'h4), .out(adder_4_out));  // open: cin, cout
  Adder #(.width(32)) adder_5 (.a(register_1_q), .b(Ii32b), .out(adder_5_out));  // open: cin, cout
  not not_11 (not_11_out, and_1_out);
  not not_12 (not_12_out, not_11_out);
  not not_13 (not_13_out, not_12_out);
  not not_14 (not_14_out, not_13_out);
  Multiplexer #(.width(5)) multiplexer_1 (
    .in0(immediate_decoder_1_rs1), .in1(immediate_decoder_1_rd), .out(multiplexer_1_out), .sel(and_1_out));  // open: en
  Multiplexer #(.width(5)) multiplexer_2 (
    .in0(immediate_decoder_1_rs2), .in1(immediate_decoder_1_rd), .out(multiplexer_2_out), .sel(and_1_out));  // open: en
  Multiplexer #(.width(32)) multiplexer_3 (
    .in0(multiplexer_4_out), .in1({immediate_decoder_1_u, {12{1'b0}}}), .out(multiplexer_3_out), .sel(LUI));  // open: en
  Multiplexer #(.width(32)) multiplexer_4 (
    .in0(multiplexer_5_out), .in1(adder_3_out), .out(multiplexer_4_out), .sel(AUIPC));  // open: en
  or or_2 (or_2_out, JALR, JAL);
  Multiplexer #(.width(32)) multiplexer_5 (
    .in0(multiplexer_9_out), .in1(adder_4_out), .out(multiplexer_5_out), .sel(or_2_out));  // open: en
  register_write register_write_1 (.in_1(opcode), .out_2(register_write_1_out_2));
  Comparator #(.width(5), .mode("unsigned")) comparator_1 (
    .a({5{1'b0}}), .b(multiplexer_1_out), .eq(comparator_1_eq));  // open: gt, lt
  Comparator #(.width(5), .mode("unsigned")) comparator_2 (
    .a({5{1'b0}}), .b(multiplexer_2_out), .eq(comparator_2_eq));  // open: gt, lt
  RAM #(.addrWidth(5), .dataWidth(32), .bus("separate")) ram_1 (
    .addr(multiplexer_1_out), .din(multiplexer_3_out), .data(ram_1_data), .str(register_write_1_out_2),
    .clk(not_14_out), .ld(1'b1));  // open: sel, clr
  RAM #(.addrWidth(5), .dataWidth(32), .bus("separate")) ram_2 (
    .addr(multiplexer_2_out), .din(multiplexer_3_out), .data(ram_2_data), .str(register_write_1_out_2),
    .clk(not_14_out), .ld(1'b1));  // open: sel, clr
  Transistor #(.\type ("n"), .width(32)) transistor_5 (.in(Ii32b), .out(transistor_5_out), .gate(ld));
  Transistor #(.\type ("n"), .width(32)) transistor_6 (.in(Si32b), .out(transistor_5_out), .gate(st));
  Pull_Resistor pull_resistor_1 (.node(transistor_5_out));
  Multiplexer #(.width(32)) multiplexer_6 (
    .in0(ram_1_data), .in1({32{1'b0}}), .out(multiplexer_6_out), .sel(comparator_1_eq));  // open: en
  Register #(.width(32), .trigger("high")) register_1 (
    .D(multiplexer_6_out), .Q(register_1_q), .clk(not_10_out));  // open: en, clr
  Multiplexer #(.width(32)) multiplexer_7 (
    .in0(ram_2_data), .in1({32{1'b0}}), .out(multiplexer_7_out), .sel(comparator_2_eq));  // open: en
  Register #(.width(32), .trigger("high")) register_2 (
    .D(multiplexer_7_out), .Q(register_2_q), .clk(not_10_out));  // open: en, clr
  Adder #(.width(32)) adder_6 (.a(transistor_5_out), .b(register_1_q), .out(adder_6_out));  // open: cin, cout
  data_in_stapler data_in_stapler_1 (
    .address(adder_6_out), .to_write(register_2_q), .current_value_at_location(ram_3_data),
    .combined_data(data_in_stapler_1_combined_data), .funct3(funct3));
  Comparator #(.width(7), .mode("unsigned")) comparator_3 (
    .a(7'b0010011), .b(opcode), .eq(comparator_3_eq));  // open: gt, lt
  branch_evaluator branch_evaluator_1 (
    .rs1(register_1_q), .rs2(register_2_q), .out_4(branch_evaluator_1_out_4), .funct3(funct3));
  Comparator #(.width(7), .mode("unsigned")) comparator_4 (
    .a(7'b1100011), .b(opcode), .eq(comparator_4_eq));  // open: gt, lt
  and and_2 (and_2_out, comparator_4_eq, branch_evaluator_1_out_4);
  Multiplexer #(.width(32)) multiplexer_8 (
    .in0(register_2_q), .in1(Ii32b), .out(multiplexer_8_out), .sel(comparator_3_eq));  // open: en
  RAM #(.addrWidth(24), .dataWidth(32), .bus("separate")) ram_3 (
    .addr(adder_6_out[25:2]), .din(data_in_stapler_1_combined_data), .data(ram_3_data), .str(st),
    .clk(not_14_out), .ld(1'b1));  // open: sel, clr
  ALU alu_1 (
    .rs1(register_1_q), .rs2(multiplexer_8_out), .immediate(comparator_3_eq), .out_6(alu_1_out_6),
    .funct7_i_think(funct7), .funct3(funct3));
  Multiplexer #(.width(32)) multiplexer_9 (
    .in0(alu_1_out_6), .in1(data_out_slicer_1_out_4), .out(multiplexer_9_out), .sel(ld));  // open: en
  data_out_slicer data_out_slicer_1 (
    .address(adder_6_out), .RAM_data(ram_3_data), .funct3(funct3), .out_4(data_out_slicer_1_out_4));

  // Notes on the sheet:
  //   splitter discards 2 least significant and 6 most significant bits
  //   control state B
  //   control state A
  //   contents of rom_1 (hex, n*v repeats v):
  //   16413*0 fd010113 2812423 2912223 3212023 1312e23 1412c23 1512a23 2112623 1612823 1712623 413 493
  //   200993 300a93 100a13 3e800913 147793 4078663 b47793 4078263 ffc40793 4f9f263 140413 ff2412e3 2c12083
  //   2812403 48513 2012903 2412483 1c12983 1812a03 1412a83 1012b03 c12b83 3010113 8067 8484b3 fbdff06f
  //   347793 fb578ee3 40b13 b93 fffb0513 1bc000ef ffeb0b13 ab8bb3 ff6a48e3 ffcb8793 100713 fff78b13 78593
  //   70513 78a63 1f4000ef 50713 b0793 fe5ff06f e484b3 f71ff06f 2197 24818193 80c18513 82818613 40a60633
  //   593 340000ef 517 22c50513 1dc000ef 290000ef 12503 410593 613 eddff0ef 1d80006f 8067 12537 127b7
  //   ba850713 ba878793 e78c63 337 30313 30663 ba850513 30067 8067 127b7 12537 ba878593 ba850793 40f585b3
  //   4025d593 1f5d793 b785b3 4015d593 58c63 337 30313 30663 ba850513 30067 8067 80c1c703 4071663 ff010113
  //   812423 112623 78413 f7dff0ef 7b7 78793 78a63 10537 77050513 ffff0097 dc0080e7 100793 80f18623 c12083
  //   812403 1010113 8067 8067 7b7 78793 2078663 125b7 10537 ff010113 bb858593 77050513 112623 ffff0097
  //   d78080e7 c12083 1010113 f39ff06f 2050c63 ff010113 50593 112623 812423 100513 fff58413 84000ef 40593
  //   fe041ae3 c12083 812403 1010113 8067 100513 8067 100793 4a7da63 ff010113 812423 912223 1212023 112623
  //   50413 493 100913 fff40513 fd5ff0ef ffe40413 a484b3 fe8948e3 c12083 812403 148513 12903 412483
  //   1010113 8067 100513 8067 50613 513 15f693 68463 c50533 15d593 161613 fe0596e3 8067 50593 693 613 513
  //   2240006f ff010113 593 812423 112623 50413 28c000ef 127b7 bac7a503 3c52783 78463 780e7 40513 380000ef
  //   ff010113 117b7 11737 812423 77870713 77c78413 40e40433 912223 1212023 112623 40245413 493 77c78913
  //   941e63 812403 c12083 412483 12903 1010113 dadff06f ffc00593 48513 f3dff0ef a90533 ffc52783 148493
  //   780e7 fc9ff06f ff010113 812423 912223 11437 114b7 77448793 77440413 40f40433 1212023 112623 40245413
  //   77448493 913 4891263 114b7 d4dff0ef 11437 77448793 77840413 40f40433 40245413 77448493 913 2891863
  //   c12083 812403 412483 12903 1010113 8067 4a783 190913 448493 780e7 fadff06f 4a783 190913 448493 780e7
  //   fc1ff06f f00313 50713 2c37e63 f77793 a079063 8059263 ff067693 f67613 e686b3 b72023 b72223 b72423
  //   b72623 1070713 fed766e3 61463 8067 40c306b3 269693 297 5686b3 c68067 b70723 b706a3 b70623 b705a3
  //   b70523 b704a3 b70423 b703a3 b70323 b702a3 b70223 b701a3 b70123 b700a3 b70023 8067 ff5f593 859693
  //   d5e5b3 1059693 d5e5b3 f6dff06f 279693 297 5686b3 8293 fa0680e7 28093 ff078793 40f70733 f60633
  //   f6c378e3 f3dff06f 127b7 bac7a703 50313 14872783 79663 14c70793 14f72423 47a703 1f00813 fff00513
  //   4e84a63 271893 2030c63 1178533 8c52423 1887a803 100613 e61633 c86833 1907a423 10d52423 200693 d31863
  //   18c7a683 c6e633 18c7a623 170713 e7a223 11787b3 b7a423 513 8067 fd010113 127b7 1312e23 bac7a983
  //   1412c23 1512a23 1612823 2112623 2812423 2912223 3212023 1712623 50a93 58a13 100b13 1489a483 48c63
  //   44a403 fff40913 241413 848433 2095863 2c12083 2812403 2412483 2012903 1c12983 1812a03 1412a83
  //   1012b03 c12b83 3010113 8067 a0c63 10442783 1478863 fff90913 ffc40413 fbdff06f 44a703 442783 fff70713
  //   3271c63 124a223 fe0780e3 1884a683 12b1733 44ab83 d776b3 2069263 780e7 44a703 1489a783 f77714e3
  //   faf48ce3 f61ff06f 42223 fcdff06f 18c4a683 8442583 d77733 71863 a8513 780e7 fcdff06f 58513 780e7
  //   fc1ff06f 593 613 693 713 793 5d00893 73 2055263 ff010113 812423 50413 112623 40800433 10000ef 852023
  //   6f 6f 8081a503 8067 1025*0 10264 10210 0 0 11a6c 11ad4 11b3c 38*0 1 0 abcd330e e66d1234 5deec b
  //   219*0 11780 11780
  //   add 2 bits on the bottom, and 6 on the top
  //   branch evaluator output
  //   rs1 + sign extended I-immediate for JALR instruction
  //   no need to set LSB to zero as bottom 2 bits will be discarded anyway
  //   JAL and JALR both write PC+4 to rd
  //   rs1 line to to add to sign extended I-immediate for JALR instruction
  //   branch is opcode 1100011
endmodule

module immediate_decoder (
  input  [31:0] in_1,
  output [4:0] rd,
  output [4:0] rs1,
  output [6:0] opcode,
  output [4:0] rs2,
  output [2:0] funct3,
  output [6:0] funct7,
  output [11:0] I,
  output [11:0] S,
  output [12:0] B,
  output [19:0] U,
  output [31:0] J
);

  assign J = {{11{in_1[31]}}, {in_1[31], in_1[19:12], in_1[20], in_1[30:21], 1'b0}};  // Bit_Extender bit_extender_1

  assign B = {in_1[31], in_1[7], in_1[30:25], in_1[11:8], 1'b0};
  assign funct3 = in_1[14:12];
  assign funct7 = in_1[31:25];
  assign I = in_1[31:20];
  assign opcode = in_1[6:0];
  assign rd = in_1[11:7];
  assign rs1 = in_1[19:15];
  assign rs2 = in_1[24:20];
  assign S = {in_1[31:25], in_1[11:7]};
  assign U = in_1[31:12];
endmodule

module jump_evaluator (
  input  [23:0] current_program_counter,
  input  [31:0] relative_J_immediate,
  input  ALU_conditional,
  output [23:0] next_program_counter_value
);
endmodule

module ALU (
  input  [6:0] funct7_i_think,
  input  [31:0] rs1,
  input  [31:0] rs2,
  input  immediate,
  input  [2:0] funct3,
  output [31:0] out_6
);

  wire and_1_out, comparator_1_gt, comparator_2_gt, not_1_out;
  wire [31:0] adder_1_out, and_2_out, bit_extender_1_out, bit_extender_2_out, multiplexer_1_out,
       multiplexer_2_out, or_1_out, shifter_1_out, shifter_2_out, shifter_3_out, subtractor_1_out, xor_1_out;

  not not_1 (not_1_out, immediate);
  Adder #(.width(32)) adder_1 (.a(rs1), .b(rs2), .out(adder_1_out));  // open: cin, cout
  Subtractor #(.width(32)) subtractor_1 (.a(rs1), .b(rs2), .out(subtractor_1_out));  // open: bin, bout
  Shifter #(.width(32)) shifter_1 (.in(rs1), .\dist (rs2[4:0]), .out(shifter_1_out));
  Comparator #(.width(32)) comparator_1 (.a(rs1), .b(rs2), .gt(comparator_1_gt));  // open: eq, lt
  Comparator #(.width(32), .mode("unsigned")) comparator_2 (.a(rs1), .b(rs2), .gt(comparator_2_gt));  // open: eq, lt
  Shifter #(.width(32), .shift("lr")) shifter_2 (.in(rs1), .\dist (rs2[4:0]), .out(shifter_2_out));
  Shifter #(.width(32), .shift("ar")) shifter_3 (.in(rs1), .\dist (rs2[4:0]), .out(shifter_3_out));
  Multiplexer #(.width(32)) multiplexer_1 (
    .in0(adder_1_out), .in1(subtractor_1_out), .out(multiplexer_1_out), .sel(and_1_out));  // open: en
  and and_1 (and_1_out, not_1_out, funct7_i_think[5]);
  assign xor_1_out = rs1 ^ rs2;  // XOR_Gate xor_1, 32 bits wide
  Multiplexer #(.width(32)) multiplexer_2 (
    .in0(shifter_2_out), .in1(shifter_3_out), .out(multiplexer_2_out), .sel(funct7_i_think[5]));  // open: en
  assign or_1_out = rs1 | rs2;  // OR_Gate or_1, 32 bits wide
  assign and_2_out = rs1 & rs2;  // AND_Gate and_2, 32 bits wide
  assign bit_extender_1_out = {{31{1'b0}}, comparator_1_gt};  // Bit_Extender bit_extender_1
  assign bit_extender_2_out = {{31{1'b0}}, comparator_2_gt};  // Bit_Extender bit_extender_2
  Multiplexer #(.select(3), .width(32)) multiplexer_3 (
    .in0(multiplexer_1_out), .in1(shifter_1_out), .in2(bit_extender_1_out), .in3(bit_extender_2_out),
    .in4(xor_1_out), .in5(multiplexer_2_out), .in6(or_1_out), .in7(and_2_out), .out(out_6), .sel(funct3));  // open: en

  // Notes on the sheet:
  //   ADD
  //   SUB
  //   SLL
  //   SLT
  //   SLTU
  //   XOR
  //   SRL
  //   SRA
  //   OR
  //   AND
  //   bit 5 of funct7 is used a lot
  //   on if rs1 < rs2
endmodule

module immediate_chooser (
  input  [6:0] opcode,
  input  [2:0] funct3,
  output I,
  output R,
  output S,
  output B,
  output U,
  output J
);

  wire comparator_1_eq, comparator_2_eq, comparator_3_eq, comparator_4_eq, comparator_5_eq, comparator_6_eq,
       comparator_9_eq, comparator_10_eq, demultiplexer_1_out0, demultiplexer_1_out1, or_1_out;

  Comparator #(.width(3)) comparator_1 (.a(funct3), .b(3'b001), .eq(comparator_1_eq));  // open: gt, lt
  Comparator #(.width(3)) comparator_2 (.a(funct3), .b(3'b101), .eq(comparator_2_eq));  // open: gt, lt
  or or_1 (or_1_out, comparator_1_eq, comparator_2_eq);
  Comparator #(.width(5)) comparator_3 (.a(opcode[6:2]), .b({5{1'b0}}), .eq(comparator_3_eq));  // open: gt, lt
  Comparator #(.width(5)) comparator_4 (.a(opcode[6:2]), .b(5'b00100), .eq(comparator_4_eq));  // open: gt, lt
  Demultiplexer demultiplexer_1 (
    .out0(demultiplexer_1_out0), .out1(demultiplexer_1_out1), .in(comparator_4_eq), .sel(or_1_out));  // open: en
  Comparator #(.width(5)) comparator_5 (.a(opcode[6:2]), .b(5'b11001), .eq(comparator_5_eq));  // open: gt, lt
  Comparator #(.width(5)) comparator_6 (.a(opcode[6:2]), .b(5'b01100), .eq(comparator_6_eq));  // open: gt, lt
  Comparator #(.width(5)) comparator_7 (.a(opcode[6:2]), .b(5'b01000), .eq(S));  // open: gt, lt
  Comparator #(.width(5)) comparator_8 (.a(opcode[6:2]), .b(5'b11000), .eq(B));  // open: gt, lt
  Comparator #(.width(5)) comparator_9 (.a(opcode[6:2]), .b(5'b01101), .eq(comparator_9_eq));  // open: gt, lt
  Comparator #(.width(5)) comparator_10 (.a(opcode[6:2]), .b(5'b00101), .eq(comparator_10_eq));  // open: gt, lt
  Comparator #(.width(5)) comparator_11 (.a(opcode[6:2]), .b(5'b11011), .eq(J));  // open: gt, lt
  or or_2 (I, comparator_3_eq, demultiplexer_1_out0, comparator_5_eq);
  or or_3 (R, demultiplexer_1_out1, comparator_6_eq);
  or or_4 (U, comparator_9_eq, comparator_10_eq);
endmodule

module branch_evaluator (
  input  [31:0] rs1,
  input  [31:0] rs2,
  input  [2:0] funct3,
  output out_4
);

  wire comparator_1_eq, comparator_1_lt, comparator_2_gt, multiplexer_1_out, undriven;

  Comparator #(.width(32)) comparator_1 (.a(rs1), .b(rs2), .eq(comparator_1_eq), .lt(comparator_1_lt));  // open: gt
  Comparator #(.width(32), .mode("unsigned")) comparator_2 (.a(rs2), .b(rs1), .gt(comparator_2_gt));  // open: eq, lt
  Multiplexer #(.select(2)) multiplexer_1 (
    .in0(comparator_1_eq), .in1(comparator_1_lt), .in2(comparator_1_lt), .in3(comparator_2_gt),
    .out(multiplexer_1_out), .sel(funct3[2:1]), .en(undriven));
  xor xor_1 (out_4, multiplexer_1_out, funct3[0]);

  // Notes on the sheet:
  //   NOTE: 010 and 011 are invalid funct3 values for branch. they are treated as if they were 100 and 101
  //   least significant bit of funct3 inverts branch
endmodule

module LUI_AUIPC_JAL_JALR (
  input  [6:0] in_1,
  output JALR,
  output JAL,
  output AUIPC,
  output LUI,
  output Load,
  output Store
);

  Comparator #(.width(7)) comparator_1 (.a(7'b1100111), .b(in_1), .eq(JALR));  // open: gt, lt
  Comparator #(.width(7)) comparator_2 (.a(7'b1101111), .b(in_1), .eq(JAL));  // open: gt, lt
  Comparator #(.width(7)) comparator_3 (.a(7'b0010111), .b(in_1), .eq(AUIPC));  // open: gt, lt
  Comparator #(.width(7)) comparator_4 (.a(7'b0110111), .b(in_1), .eq(LUI));  // open: gt, lt
  Comparator #(.width(7)) comparator_5 (.a(7'b0000011), .b(in_1), .eq(Load));  // open: gt, lt
  Comparator #(.width(7)) comparator_6 (.a(7'b0100011), .b(in_1), .eq(Store));  // open: gt, lt
endmodule

module register_write (
  input  [6:0] in_1,
  output out_2
);

  wire comparator_1_eq, comparator_2_eq, comparator_3_eq, comparator_4_eq, comparator_5_eq, comparator_6_eq,
       comparator_7_eq;

  Comparator #(.width(7)) comparator_1 (.a(7'b0000011), .b(in_1), .eq(comparator_1_eq));  // open: gt, lt
  Comparator #(.width(7)) comparator_2 (.a(7'b1100111), .b(in_1), .eq(comparator_2_eq));  // open: gt, lt
  Comparator #(.width(7)) comparator_3 (.a(7'b1101111), .b(in_1), .eq(comparator_3_eq));  // open: gt, lt
  Comparator #(.width(7)) comparator_4 (.a(7'b0010111), .b(in_1), .eq(comparator_4_eq));  // open: gt, lt
  Comparator #(.width(7)) comparator_5 (.a(7'b0110111), .b(in_1), .eq(comparator_5_eq));  // open: gt, lt
  Comparator #(.width(7), .mode("unsigned")) comparator_6 (
    .a(7'b0010011), .b(in_1), .eq(comparator_6_eq));  // open: gt, lt
  Comparator #(.width(7), .mode("unsigned")) comparator_7 (
    .a(7'b0110011), .b(in_1), .eq(comparator_7_eq));  // open: gt, lt
  or or_1 (out_2, comparator_2_eq, comparator_3_eq, comparator_4_eq, comparator_1_eq, comparator_5_eq, comparator_6_eq, comparator_7_eq);

  // Notes on the sheet:
  //   0110111, 0010111, 1101111, 1100111, 0010011, 0110011, 0000011 all write to registers
endmodule

module RAM_addresser (
  input  [31:0] rs1_val,
  output [23:0] out_2
);
endmodule

module data_out_slicer (
  input  [2:0] funct3,
  input  [31:0] address,
  input  [31:0] RAM_data,
  output [31:0] out_4
);

  wire not_1_out, not_2_out;
  wire [1:0] subtractor_1_out;
  wire [7:0] multiplexer_2_out;
  wire [15:0] multiplexer_1_out;
  wire [31:0] bit_extender_1_out, bit_extender_2_out, bit_extender_3_out, bit_extender_4_out,
       multiplexer_3_out, multiplexer_4_out, multiplexer_5_out;

  // Probe on address[1:0]
  Subtractor #(.width(2)) subtractor_1 (.a(2'b11), .b(address[1:0]), .out(subtractor_1_out));  // open: bin, bout
  not not_1 (not_1_out, address[0]);
  Multiplexer #(.width(16)) multiplexer_1 (
    .in0(RAM_data[31:16]), .in1(RAM_data[15:0]), .out(multiplexer_1_out), .sel(not_1_out));  // open: en
  Multiplexer #(.select(2), .width(8)) multiplexer_2 (
    .in0(RAM_data[31:24]), .in1(RAM_data[23:16]), .in2(RAM_data[15:8]), .in3(RAM_data[7:0]),
    .out(multiplexer_2_out), .sel(subtractor_1_out));  // open: en
  assign bit_extender_1_out = {{16{multiplexer_1_out[15]}}, multiplexer_1_out};  // Bit_Extender bit_extender_1
  Multiplexer #(.width(32)) multiplexer_3 (
    .in0(bit_extender_1_out), .in1(bit_extender_2_out), .out(multiplexer_3_out), .sel(funct3[2]));  // open: en
  assign bit_extender_2_out = {{16{1'b0}}, multiplexer_1_out};  // Bit_Extender bit_extender_2
  assign bit_extender_3_out = {{24{multiplexer_2_out[7]}}, multiplexer_2_out};  // Bit_Extender bit_extender_3
  Multiplexer #(.width(32)) multiplexer_4 (
    .in0(bit_extender_3_out), .in1(bit_extender_4_out), .out(multiplexer_4_out), .sel(funct3[2]));  // open: en
  assign bit_extender_4_out = {{24{1'b0}}, multiplexer_2_out};  // Bit_Extender bit_extender_4
  not not_2 (not_2_out, funct3[0]);
  Multiplexer #(.width(32)) multiplexer_5 (
    .in0(multiplexer_3_out), .in1(multiplexer_4_out), .out(multiplexer_5_out), .sel(not_2_out));  // open: en
  Multiplexer #(.width(32)) multiplexer_6 (
    .in0(multiplexer_5_out), .in1(RAM_data), .out(out_4), .sel(funct3[1]));  // open: en
endmodule

module data_in_stapler (
  input  [2:0] funct3,
  input  [31:0] address,
  input  [31:0] to_write,
  input  [31:0] current_value_at_location,
  output [31:0] combined_data
);

  wire [7:0] bit_extender_2_out, bitselector_2_out;
  wire [15:0] bit_extender_1_out, bitselector_1_out;
  wire [31:0] adder_1_out, adder_2_out, bit_extender_3_out, bit_extender_4_out, bit_extender_5_out,
       bit_extender_6_out, shifter_1_out, shifter_2_out, shifter_3_out, shifter_4_out, subtractor_1_out,
       subtractor_2_out;

  Bit_Extender #(.in_width(32)) bit_extender_1 (.in(to_write), .out(bit_extender_1_out));
  Bit_Extender #(.in_width(32), .out_width(8)) bit_extender_2 (.in(to_write), .out(bit_extender_2_out));
  assign bit_extender_3_out = {{16{1'b0}}, bitselector_1_out};  // Bit_Extender bit_extender_3
  BitSelector #(.width(32), .group(16)) bitselector_1 (
    .in(current_value_at_location), .out(bitselector_1_out), .sel(address[0]));
  assign bit_extender_4_out = {{16{1'b0}}, bit_extender_1_out};  // Bit_Extender bit_extender_4
  BitSelector #(.width(32), .group(8)) bitselector_2 (
    .in(current_value_at_location), .out(bitselector_2_out), .sel(address[1:0]));
  assign bit_extender_5_out = {{24{1'b0}}, bitselector_2_out};  // Bit_Extender bit_extender_5
  assign bit_extender_6_out = {{24{1'b0}}, bit_extender_2_out};  // Bit_Extender bit_extender_6
  Shifter #(.width(32)) shifter_1 (.in(bit_extender_3_out), .\dist ({address[0], 4'b0000}), .out(shifter_1_out));
  Shifter #(.width(32)) shifter_2 (.in(bit_extender_4_out), .\dist ({address[0], 4'b0000}), .out(shifter_2_out));
  Shifter #(.width(32)) shifter_3 (.in(bit_extender_5_out), .\dist ({address[1:0], 3'b000}), .out(shifter_3_out));
  Shifter #(.width(32)) shifter_4 (.in(bit_extender_6_out), .\dist ({address[1:0], 3'b000}), .out(shifter_4_out));
  Subtractor #(.width(32)) subtractor_1 (
    .a(current_value_at_location), .b(shifter_1_out), .out(subtractor_1_out));  // open: bin, bout
  Subtractor #(.width(32)) subtractor_2 (
    .a(current_value_at_location), .b(shifter_3_out), .out(subtractor_2_out));  // open: bin, bout
  Adder #(.width(32)) adder_1 (.a(subtractor_2_out), .b(shifter_4_out), .out(adder_1_out));  // open: cin, cout
  // Probe on adder_2_out
  Adder #(.width(32)) adder_2 (.a(subtractor_1_out), .b(shifter_2_out), .out(adder_2_out));  // open: cin, cout
  // Probe on adder_1_out
  Multiplexer #(.select(2), .width(32)) multiplexer_1 (
    .in0(adder_1_out), .in1(adder_2_out), .in2(to_write), .in3({32{1'b0}}), .out(combined_data),
    .sel(funct3[1:0]));  // open: en
endmodule
